// Logisim project cpu.circ as structural Verilog: 2 circuits, main circuit main
module main (
  input  [15:0] INSTRUCTION,
  input  CLOCK,
  output [15:0] FETCH_ADDRESS,
  output Overflow,
  output [15:0] s0_Value,
  output [15:0] s1_Value,
  output [15:0] s2_Value,
  output [15:0] ra_Value,
  output [15:0] sp_Value,
  output [15:0] HI_Value,
  output [15:0] LO_Value
);

  wire MEM_p1, MEM_p3, MEM_p6, MEM_p9, MEM_p12;

  Register #(.width(16)) PC ();  // open: D, en, Q, clk, clr
  Register #(.width(16)) LO ();  // open: D, en, Q, clk, clr
  Register #(.width(16)) HI ();  // open: D, en, Q, clk, clr
  // regfile_main main_1: pin names not known
  // alu_main main_2: pin names not known
  // mem_main MEM: pin names not known; wires that end beside it: MEM_p1, s0_Value, MEM_p3, MEM_p3, s1_Value, MEM_p6, MEM_p6, s2_Value, MEM_p9, MEM_p9, ra_Value, MEM_p12, MEM_p12, sp_Value

  // Other names for the same wires on the sheet: clk = CLOCK; fetch_addr[15:0] = FETCH_ADDRESS

  // Notes on the sheet:
  //   Output
  //   These are outputs/inputs from run.circ
  //   Inputs
  //   These are DEBUG/TEST outputs from your circuit.
endmodule

module control_signal (
  input  [3:0] in_1,
  output Branch,
  output Jump,
  output RegDst,
  output MemRead,
  output MemToReg,
  output MemWrite
);

  wire addi, addiu, andi, beq, bne, J, Jr, lui, mfhi, mflo, or_3_out, ori, Rtype, slti;

  Comparator #(.width(4)) comparator_1 (.a(in_1), .b(4'b0000), .eq(Rtype));  // open: gt, lt
  Comparator #(.width(4)) comparator_2 (.a(in_1), .b(4'b0001), .eq(lui));  // open: gt, lt
  Comparator #(.width(4)) comparator_3 (.a(in_1), .b(4'b0010), .eq(J));  // open: gt, lt
  Comparator #(.width(4)) comparator_4 (.a(in_1), .b(4'b0011), .eq(Jr));  // open: gt, lt
  Comparator #(.width(4)) comparator_5 (.a(in_1), .b(4'b0100), .eq(beq));  // open: gt, lt
  Comparator #(.width(4)) comparator_6 (.a(in_1), .b(4'b0101), .eq(bne));  // open: gt, lt
  Comparator #(.width(4)) comparator_7 (.a(in_1), .b(4'b0110), .eq(addi));  // open: gt, lt
  Comparator #(.width(4)) comparator_8 (.a(in_1), .b(4'b0111), .eq(addiu));  // open: gt, lt
  Comparator #(.width(4)) comparator_9 (.a(in_1), .b(4'b1000), .eq(slti));  // open: gt, lt
  Comparator #(.width(4)) comparator_10 (.a(in_1), .b(4'b1001), .eq(andi));  // open: gt, lt
  Comparator #(.width(4)) comparator_11 (.a(in_1), .b(4'b1010), .eq(ori));  // open: gt, lt
  Comparator #(.width(4)) comparator_12 (.a(in_1), .b(4'b1011), .eq(MemRead));  // open: gt, lt
  Comparator #(.width(4)) comparator_13 (.a(in_1), .b(4'b1100), .eq(MemWrite));  // open: gt, lt
  Comparator #(.width(4)) comparator_14 (.a(in_1), .b(4'b1101), .eq(mfhi));  // open: gt, lt
  Comparator #(.width(4)) comparator_15 (.a(in_1), .b(4'b1110), .eq(mflo));  // open: gt, lt
  or or_1 (Branch, beq, bne);
  or or_2 (Jump, J, Jr);
  or or_3 (or_3_out, Rtype, mfhi);
  or or_4 (RegDst, or_3_out, mflo);

  assign MemToReg = MemRead;

  // Other names for the same wires on the sheet: lh = MemRead; sh = MemWrite
endmodule
